// Logisim project control-logic.circ as structural Verilog: 1 circuit, main circuit control_logic
module control_logic (
  input  [31:0] Instruction,
  input  BrEq,
  input  BrLt,
  output PCSel,
  output RegWEn,
  output [2:0] ImmSel,
  output BrUn,
  output ASel,
  output BSel,
  output [3:0] ALUSel,
  output MemWEn,
  output [1:0] WBSel
);

  wire add000, and111, and_1_out, and_2_out, and_3_out, and_4_out, and_5_out, and_6_out, auipc, beq000,
       bge101, bgeu111, blt100, bltu110, bne001, comparator_1_eq, comparator_2_eq, comparator_11_eq,
       comparator_14_eq, comparator_15_eq, comparator_16_eq, comparator_17_eq, comparator_18_eq,
       demultiplexer_4_out0, demultiplexer_4_out1, demultiplexer_4_out3, demultiplexer_4_out5,
       demultiplexer_7_out0, demultiplexer_9_out0, demultiplexer_9_out1, demultiplexer_9_out4,
       demultiplexer_9_out5, demultiplexer_9_out6, demultiplexer_9_out7, jal, jalr, lb, lh, lui, lw, mul000,
       mulh, mulhu, not_1_out, not_2_out, not_3_out, or110, or_1_out, priority_encoder_1_p9,
       priority_encoder_1_p10, priority_encoder_1_p11, priority_encoder_1_p12, priority_encoder_1_p13,
       priority_encoder_1_p14, priority_encoder_1_p15, priority_encoder_1_p16, sb, sh, sll001, slt010,
       sra101, srl101, sub001, sw, xor100;
  wire [5:0] priority_encoder_1_p25;
  wire [15:14] rom_1_data;

  Comparator #(.mode("unsigned"), .width(7)) comparator_1 (
    .a(7'b0000011), .b(Instruction[6:0]), .eq(comparator_1_eq));  // open: gt, lt
  Comparator #(.mode("unsigned"), .width(7)) comparator_2 (
    .a(7'b0100011), .b(Instruction[6:0]), .eq(comparator_2_eq));  // open: gt, lt
  Comparator #(.mode("unsigned"), .width(7)) comparator_3 (
    .a(7'b0110111), .b(Instruction[6:0]), .eq(lui));  // open: gt, lt
  Comparator #(.mode("unsigned"), .width(7)) comparator_4 (
    .a(7'b0010111), .b(Instruction[6:0]), .eq(auipc));  // open: gt, lt
  Comparator #(.mode("unsigned"), .width(7)) comparator_5 (
    .a(7'b1100111), .b(Instruction[6:0]), .eq(jalr));  // open: gt, lt
  Comparator #(.mode("unsigned"), .width(7)) comparator_6 (
    .a(7'b1101111), .b(Instruction[6:0]), .eq(jal));  // open: gt, lt
  ROM #(.addrWidth(6), .dataWidth(16)) rom_1 (
    .addr(priority_encoder_1_p25),
    .data({rom_1_data, WBSel, MemWEn, ALUSel, BSel, ASel, BrUn, ImmSel, RegWEn}));
  Demultiplexer #(.select(3)) demultiplexer_1 (
    .out0(lb), .out1(lh), .out2(lw), .in(comparator_1_eq), .sel(Instruction[14:12]));  // open: out3, out4, out5, out6, out7
  Demultiplexer #(.select(3)) demultiplexer_2 (
    .out0(sb), .out1(sh), .out2(sw), .in(comparator_2_eq), .sel(Instruction[14:12]));  // open: out3, out4, out5, out6, out7
  // Priority_Encoder #(.select_enc(6)) priority_encoder_1: pin names not known; wires that end beside it: xor100, srl101, sra101, or110, and111, lb, lh, lw, priority_encoder_1_p9, priority_encoder_1_p10, priority_encoder_1_p11, priority_encoder_1_p12, priority_encoder_1_p13, priority_encoder_1_p14, priority_encoder_1_p15, priority_encoder_1_p16, sb, sh, sw, beq000, bne001, blt100, bge101, bltu110, priority_encoder_1_p25, bgeu111, auipc, lui, jal, jalr
  Comparator #(.mode("unsigned"), .width(10)) comparator_7 (
    .a(10'h13), .b({Instruction[14:12], Instruction[6:0]}), .eq(priority_encoder_1_p9));  // open: gt, lt
  Comparator #(.mode("unsigned"), .width(10)) comparator_8 (
    .a(10'h93), .b({Instruction[14:12], Instruction[6:0]}), .eq(priority_encoder_1_p10));  // open: gt, lt
  Comparator #(.mode("unsigned"), .width(10)) comparator_9 (
    .a(10'h113), .b({Instruction[14:12], Instruction[6:0]}), .eq(priority_encoder_1_p11));  // open: gt, lt
  Comparator #(.mode("unsigned"), .width(10)) comparator_10 (
    .a(10'h213), .b({Instruction[14:12], Instruction[6:0]}), .eq(priority_encoder_1_p12));  // open: gt, lt
  Demultiplexer demultiplexer_3 (
    .out0(priority_encoder_1_p13), .out1(priority_encoder_1_p14), .in(comparator_11_eq), .sel(Instruction[30]));
  Comparator #(.mode("unsigned"), .width(10)) comparator_11 (
    .a(10'h293), .b({Instruction[14:12], Instruction[6:0]}), .eq(comparator_11_eq));  // open: gt, lt
  Comparator #(.mode("unsigned"), .width(10)) comparator_12 (
    .a(10'h313), .b({Instruction[14:12], Instruction[6:0]}), .eq(priority_encoder_1_p15));  // open: gt, lt
  Comparator #(.mode("unsigned"), .width(10)) comparator_13 (
    .a(10'h393), .b({Instruction[14:12], Instruction[6:0]}), .eq(priority_encoder_1_p16));  // open: gt, lt
  Demultiplexer #(.select(3)) demultiplexer_4 (
    .out0(demultiplexer_4_out0), .out1(demultiplexer_4_out1), .out2(slt010), .out3(demultiplexer_4_out3),
    .out4(xor100), .out5(demultiplexer_4_out5), .out6(or110), .out7(and111), .in(comparator_14_eq),
    .sel(Instruction[14:12]));
  Comparator #(.mode("unsigned"), .width(7)) comparator_14 (
    .a(7'b0110011), .b(Instruction[6:0]), .eq(comparator_14_eq));  // open: gt, lt
  Demultiplexer #(.select(3)) demultiplexer_5 (
    .out0(beq000), .out1(bne001), .out4(blt100), .out5(bge101), .out6(bltu110), .out7(bgeu111),
    .in(comparator_15_eq), .sel(Instruction[14:12]));  // open: out2, out3
  Comparator #(.mode("unsigned"), .width(7)) comparator_15 (
    .a(7'b1100011), .b(Instruction[6:0]), .eq(comparator_15_eq));  // open: gt, lt
  Demultiplexer demultiplexer_6 (.out0(add000), .out1(mul000), .in(demultiplexer_7_out0), .sel(Instruction[25]));
  Demultiplexer demultiplexer_7 (
    .out0(demultiplexer_7_out0), .out1(sub001), .in(demultiplexer_4_out0), .sel(Instruction[30]));
  Demultiplexer demultiplexer_8 (.out0(sll001), .out1(mulh), .in(demultiplexer_4_out1), .sel(Instruction[25]));
  Comparator #(.mode("unsigned"), .width(7)) comparator_16 (
    .a(7'b1100011), .b(Instruction[6:0]), .eq(comparator_16_eq));  // open: gt, lt
  Demultiplexer #(.select(3)) demultiplexer_9 (
    .out0(demultiplexer_9_out0), .out1(demultiplexer_9_out1), .out4(demultiplexer_9_out4),
    .out5(demultiplexer_9_out5), .out6(demultiplexer_9_out6), .out7(demultiplexer_9_out7),
    .in(comparator_16_eq), .sel(Instruction[14:12]));  // open: out2, out3
  Demultiplexer demultiplexer_10 (.out1(mulhu), .in(demultiplexer_4_out3), .sel(Instruction[25]));  // open: out0
  and and_1 (and_1_out, BrEq, demultiplexer_9_out0);
  not not_1 (not_1_out, BrEq);
  and and_2 (and_2_out, not_1_out, demultiplexer_9_out1);
  and and_3 (and_3_out, demultiplexer_9_out5, not_2_out);
  not not_2 (not_2_out, BrLt);
  and and_4 (and_4_out, demultiplexer_9_out6, BrLt);
  and and_5 (and_5_out, demultiplexer_9_out7, not_3_out);
  not not_3 (not_3_out, BrLt);
  Demultiplexer demultiplexer_11 (.out0(srl101), .out1(sra101), .in(demultiplexer_4_out5), .sel(Instruction[30]));
  and and_6 (and_6_out, demultiplexer_9_out4, BrLt);
  ExactlyOne xor_1 (
    .out(PCSel), .in0(and_1_out), .in1(and_2_out), .in2(and_6_out), .in3(and_3_out), .in4(and_4_out),
    .in5(and_5_out), .in6(or_1_out));
  Comparator #(.mode("unsigned"), .width(7)) comparator_17 (
    .a(7'b1100111), .b(Instruction[6:0]), .eq(comparator_17_eq));  // open: gt, lt
  Comparator #(.mode("unsigned"), .width(7)) comparator_18 (
    .a(7'b1101111), .b(Instruction[6:0]), .eq(comparator_18_eq));  // open: gt, lt
  or or_1 (or_1_out, comparator_17_eq, comparator_18_eq);

  // Other names for the same wires on the sheet: opcode[6:0] = Instruction[6:0]; funct3[2:0] = Instruction[14:12];
  //   funct7[6:0] = Instruction[31:25]

  // Notes on the sheet:
  //   INPUTS to your circuit
  //   Connect ROM Input here ->
  //   I and I* control
  //   contents of rom_1 (hex, n*v repeats v):
  //   1001 1401 1601 1081 1401 1401 1101 1201 1281 1681 1301 1381 41 41 41 1041 10c1 1141 1241 12c1 16c1
  //   1341 13c1 844 844 844 4*1066 1076 1076 1069 17c9 206b 2041 0 0 4*6 16 16
  //   ROM FOR CONTROL LOGIC
  //   DON'T CHANGE THE LOCATIONS OF THE INPUTS AND OUTPUTS!
  //   This is only if you choose to do the ROM option
  //   OUTPUT from your circuit
  //   Reminder: If using ROM, use combinational logic for PCSel
endmodule
