// Logisim project cpu.circ as structural Verilog: 1 circuit, main circuit cpu
module cpu (
  input  clk,
  input  [31:0] Instruction,
  input  [31:0] MemReadData,
  output [31:0] MemAddress,
  output [31:0] ProgramCounter,
  output [31:0] ra,
  output [31:0] sp,
  output [31:0] t0,
  output [31:0] t1,
  output [31:0] t2,
  output [31:0] s0,
  output [31:0] s1,
  output [31:0] a0,
  output [3:0] MemWriteMask,
  output [31:0] MemWriteData
);

  wire ASel, branch_comp_1_p4, BrEq, BrLt, BrUn, BSel, MemWEn, PCSel, RegWEn;
  wire [1:0] WBSel;
  wire [2:0] control_logic_1_immsel;
  wire [3:0] ALUSel;
  wire [31:0] adder_1_out, BrData1, BrData2, imm_gen_1_immediate, Instruction_Piped, multiplexer_1_out,
       partial_load_1_datatoreg, PCP4, register_1_q, register_6_q, test, test1, test2, WriteData;

  Adder #(.width(32)) adder_1 (.a(ProgramCounter), .b(32'h4), .out(adder_1_out));  // open: cin, cout
  Register #(.width(32)) register_1 (.D(ProgramCounter), .en(1'b1), .clk(clk), .Q(register_1_q));  // open: clr
  Multiplexer #(.width(32)) multiplexer_1 (.in0(adder_1_out), .in1(MemAddress), .out(multiplexer_1_out), .sel(PCSel));
  Adder #(.width(32)) adder_2 (.a(register_1_q), .b(32'h4), .out(PCP4));  // open: cin, cout
  Register #(.width(32)) PC (.D(multiplexer_1_out), .en(1'b1), .clk(clk), .Q(ProgramCounter));  // open: clr
  Register #(.width(32)) register_2 (.D(test1), .en(1'b1), .clk(clk));  // open: Q, clr
  Register #(.width(32)) register_3 (.D(test), .en(1'b1), .clk(clk));  // open: Q, clr
  Register #(.width(32)) register_4 (.D(Instruction), .clk(clk), .Q(Instruction_Piped));  // open: en, clr
  Register #(.width(32)) register_5 (.D(test2), .en(1'b1), .clk(clk));  // open: Q, clr
  control_logic control_logic_1 (
    .Instruction(Instruction_Piped), .BrEq(BrEq), .BrLt(BrLt), .PCSel(PCSel), .RegWEn(RegWEn),
    .ImmSel(control_logic_1_immsel), .BrUn(BrUn), .ASel(ASel), .BSel(BSel), .ALUSel(ALUSel), .MemWEn(MemWEn),
    .WBSel(WBSel));
  regfile regfile_1 (
    .ReadIndex1(Instruction_Piped[19:15]), .ReadIndex2(Instruction_Piped[24:20]),
    .WriteIndex(Instruction_Piped[11:7]), .WriteData(WriteData), .RegWEn(RegWEn), .clk(clk), .ra(ra),
    .sp(sp), .t0(t0), .t1(t1), .t2(t2), .s0(s0), .s1(s1), .a0(a0), .ReadData1(BrData1), .ReadData2(BrData2));
  imm_gen imm_gen_1 (.Instruction(Instruction_Piped), .ImmSel(control_logic_1_immsel), .Immediate(imm_gen_1_immediate));
  Multiplexer #(.width(32)) multiplexer_2 (.in0(BrData2), .in1(imm_gen_1_immediate), .out(test), .sel(BSel));
  Register #(.width(32)) register_6 (.D(ProgramCounter), .clk(clk), .Q(register_6_q));  // open: en, clr
  Multiplexer #(.width(32)) multiplexer_3 (.in0(BrData1), .in1(register_6_q), .out(test1), .sel(ASel));
  // branch_comp branch_comp_1: pin names not known; wires that end beside it: BrData1, BrData2, BrUn, branch_comp_1_p4, branch_comp_1_p4, BrEq, BrLt
  alu alu_1 (.A(test1), .B(test), .ALUSel(ALUSel), .ALUResult(MemAddress));
  partial_load partial_load_1 (
    .Instruction(Instruction_Piped), .MemAddress(MemAddress), .DataFromMem(MemReadData),
    .DataToReg(partial_load_1_datatoreg));
  partial_store partial_store_1 (
    .Instruction(Instruction_Piped), .MemAddress(MemAddress), .DataFromReg(BrData2), .MemRW(MemWEn),
    .MemWriteMask(MemWriteMask), .DataToMem(MemWriteData));
  Multiplexer #(.select(2), .width(32)) multiplexer_4 (
    .in0(partial_load_1_datatoreg), .in1(MemAddress), .in2(PCP4), .out(WriteData), .sel(WBSel));  // open: in3

  // Other names for the same wires on the sheet: PCUpdate[31:0] = MemAddress

  // Notes on the sheet:
  //   To IMEM
  //   IMEM (do **NOT** move this)
  //   From IMEM
  //   Inputs/Outputs for testing. Do **NOT** move these.
  //   To DMEM
  //   DMEM (do **NOT** move this)
  //   From DMEM
endmodule
