// Logisim project imm-gen.circ as structural Verilog: 1 circuit, main circuit imm_gen
module imm_gen (
  input  [31:0] Instruction,
  input  [2:0] ImmSel,
  output [31:0] Immediate
);

  wire [31:0] shifter_1_out, shifter_2_out, shifter_3_out, shifter_4_out;

  Shifter #(.shift("ar"), .width(32)) shifter_1 (.in(Instruction), .\dist (5'b10100), .out(shifter_1_out));
  Shifter #(.shift("ar"), .width(32)) shifter_2 (
    .in({Instruction[31:25], Instruction[11:7], {20{1'b0}}}), .\dist (5'b10100), .out(shifter_2_out));
  Shifter #(.shift("ar"), .width(32)) shifter_3 (
    .in({Instruction[31], Instruction[7], Instruction[30:25], Instruction[11:8], {20{1'b0}}}),
    .\dist (5'b10011), .out(shifter_3_out));
  Shifter #(.shift("ar"), .width(32)) shifter_4 (
    .in({Instruction[31], Instruction[19:12], Instruction[20], Instruction[30:21], {12{1'b0}}}),
    .\dist (5'b01011), .out(shifter_4_out));
  Multiplexer #(.select(3), .width(32)) multiplexer_1 (
    .in0(shifter_1_out), .in1({{27{1'b0}}, Instruction[24:20]}), .in2(shifter_2_out), .in3(shifter_3_out),
    .in4({Instruction[31:12], {12{1'b0}}}), .in5(shifter_4_out), .out(Immediate), .sel(ImmSel));  // open: in6, in7

  // Notes on the sheet:
  //   INPUTS to your circuit
  //   001: I*
  //   010: S
  //   011: B
  //   100: U
  //   101: J
  //   000: I
  //   DON'T CHANGE THE LOCATIONS OF THE INPUTS AND OUTPUTS!
  //   OUTPUT from your circuit
endmodule
