// Logisim project test.circ as structural Verilog: 1 circuit, main circuit run_main
module run_main (
  output [31:0] ra,
  output [31:0] sp,
  output [31:0] t0,
  output [31:0] t1,
  output [31:0] t2,
  output [31:0] s0,
  output [31:0] s1,
  output [31:0] a0,
  output [31:0] RequestedAddress,
  output [31:0] RequestedInstruction,
  output [15:0] TimeStep,
  output halt
);

  wire clk;

  Clock clock_1 (.out(clk));
  // Probe on RequestedAddress
  // cpu_harness cpu_harness_1: pin names not known; wires that end beside it: RequestedInstruction, clk, RequestedAddress, ra, sp, t0, t1, t2, s0, s1, a0
  ROM #(.addrWidth(14), .dataWidth(32)) rom_1 (.addr(RequestedAddress[15:2]), .data(RequestedInstruction));
  // Probe on RequestedInstruction
  Counter #(.max('hffff), .width(16)) counter_1 (.clk(clk), .Q(TimeStep));  // open: clr, load, up, count, D, carry
  Comparator #(.width(16)) comparator_1 (.a(TimeStep), .b(16'h38), .eq(halt));  // open: gt, lt

  // Other names for the same wires on the sheet: Instruction[31:0] = RequestedInstruction;
  //   ProgramCounter[31:0] = RequestedAddress

  // Notes on the sheet:
  //   contents of rom_1 (hex, n*v repeats v):
  //   1700093 170f293 12c093 10d093 4032d093 4010d093 10a093 200313 1300b3 406080b3 50f3b3 53e0b3 53c0b3
  //   6090b3 60d0b3 60a0b3 26080b3 fe908093 60a0b3 26080b3 108093 c800413 5f600493 c800413 152634b7
  //   74848493 4942823 5042503 4941823 5042503 4941923 5042503 4940823 5042503 49408a3 5042503 4940923
  //   5042503 49409a3 5042503 f2942a23 f3442503 f2941a23 f3442503 f2941b23 f3442503 f2940a23 f3442503
  //   f2940aa3 f3442503 f2940b23 f3442503 f2940ba3 f3442503
  //   Instruction Memory
  //   Halts Execution After Constant # of Clock Cycles
  //   Constant
endmodule
