// Logisim project imm-gen-b-type.circ as structural Verilog: 1 circuit, main circuit main
module main (
  output [7:0] Test,
  output [31:0] Immediate,
  output halt,
  output [31:0] Instruction,
  output [2:0] ImmSel
);

  wire clock_1_out;
  wire [7:0] adder_1_out;

  Clock clock_1 (.out(clock_1_out));
  Adder adder_1 (.a(8'h1), .b(Test), .out(adder_1_out));  // open: cin, cout
  Register register_1 (.D(adder_1_out), .clk(clock_1_out), .Q(Test));  // open: en, clr
  ROM #(.dataWidth(32)) rom_1 (.addr(Test), .data(Instruction));
  Comparator comparator_1 (.a(Test), .b(8'h4), .eq(halt));  // open: gt, lt
  // Probe on ImmSel
  // Probe on Instruction
  ROM #(.dataWidth(3)) rom_2 (.addr(Test), .data(ImmSel));
  imm_gen imm_gen_1 (.Instruction(Instruction), .ImmSel(ImmSel), .Immediate(Immediate));

  // Notes on the sheet:
  //   contents of rom_1 (hex, n*v repeats v):
  //   7e000fe3 de000fe3 3c04d063 7e84f033
  //   Your imm_gen must fit here!
  //   contents of rom_2 (hex, n*v repeats v):
  //   3 3 3 3
  //   There should be no red or blue wires, and the result should not be all X's
endmodule
